// Digital circuit Projet1_Etape2.dig as structural Verilog
module Projet1_Etape2 (
  input  C,
  input  B,
  input  A,
  output S
);

  wire nand_1_out, nand_2_out, nand_3_out, nand_4_out, not_1_out;

  nand nand_1 (nand_1_out, ~C, B, ~A);  // NAnd
  nand nand_2 (nand_2_out, C, ~B, A);  // NAnd
  nand nand_3 (nand_3_out, C, B, ~A);  // NAnd
  nand nand_4 (nand_4_out, nand_1_out, nand_2_out);
  not not_1 (not_1_out, nand_4_out);
  nand nand_5 (S, not_1_out, nand_3_out);
endmodule
