// Digital circuit Projet2_Etape2.dig as structural Verilog
module Projet2_Etape2 (
  input  in_1,
  input  in_2,
  input  in_3,
  input  in_5,
  output out_4
);

  wire and_1_out, and_2_out, and_3_out;

  and and_1 (and_1_out, in_1, ~in_2, in_3, ~in_5);  // And
  and and_2 (and_2_out, in_1, in_2, in_3, in_5);
  and and_3 (and_3_out, ~in_1, in_2, ~in_3, in_5);  // And
  or or_1 (out_4, and_1_out, and_2_out, and_3_out);
endmodule
