// Digital circuit Projet1_Comparaison.dig as structural Verilog
module Projet1_Comparaison (
  input  A,
  input  B,
  input  C,
  input  in_6,
  input  in_7,
  input  in_8,
  output S,
  output Cout,
  output out_9,
  output out_10
);

  wire and_1_out, and_2_out, and_3_out, and_4_out, and_5_out, or_1_out, xor_1_out, xor_2_out;

  xor xor_1 (xor_1_out, A, B);
  and and_1 (and_1_out, A, B);
  xor xor_2 (xor_2_out, in_6, in_7);
  and and_2 (and_2_out, in_6, in_8);
  and and_3 (and_3_out, in_8, in_7);
  and and_4 (and_4_out, in_7, in_6);
  xor xor_3 (out_9, xor_2_out, in_8);
  xor xor_4 (S, xor_1_out, C);
  and and_5 (and_5_out, xor_1_out, C);
  or or_1 (or_1_out, and_3_out, and_4_out);
  or or_2 (out_10, and_2_out, or_1_out);
  or or_3 (Cout, and_5_out, and_1_out);
endmodule
