// Digital circuit projet1.dig as structural Verilog
module projet1 (
  input  N3,
  input  N2,
  input  N1,
  input  N0
);

  wire multiplexer_1_out, not_1_out;

  not not_1 (not_1_out, N0);
  Multiplexer #(.Selector_Bits(3)) multiplexer_1 (
    .sel({N1, N2, N3}), .in_0(not_1_out), .in_1(1'b1), .in_2(N0), .in_3(1'b1), .in_4(1'b1), .in_5(1'b1),
    .in_6(1'b1), .in_7(1'b1), .out(multiplexer_1_out));
  Seven_Seg #(.commonConnectionType("anode")) seven_seg_1 (
    .a(multiplexer_1_out), .b(1'b0), .c(1'b0), .d(1'b0), .e(1'b0), .f(1'b0), .g(1'b0), .dp(1'b0));
endmodule
